// Logisim project assignment.circ as structural Verilog: 1 circuit, main circuit main
module main (
  input  in_1
);

  wire A_2_out, A_3_out, A_out, and_1_out, and_2_out, and_3_out, and_4_out, and_5_out, and_6_out, and_7_out,
       and_8_out, B_2_out, B_out, clock_1_out, d_ff_1_q, d_ff_1_qn, d_ff_2_q, d_ff_2_qn, d_ff_3_q, d_ff_3_qn,
       d_ff_4_q, d_ff_4_qn, d_ff_5_q, d_ff_5_qn, d_ff_6_q, d_ff_6_qn, d_ff_7_q, d_ff_7_qn, d_ff_8_q,
       d_ff_8_qn, d_ff_9_q, d_ff_9_qn, d_ff_10_q, d_ff_10_qn, d_ff_11_qn, nand_1_out, nand_2_out, not_1_out,
       not_2_out, not_3_out, or_1_out, or_2_out, R_2_out, R_out, xor_1_out, xor_2_out;

  Clock clock_1 (.out(clock_1_out));
  Button A (.out(A_out));
  Button R (.out(R_out));
  Button B (.out(B_out));
  Button A_2 (.out(A_2_out));
  Button R_2 (.out(R_2_out));
  xor xor_1 (xor_1_out, clock_1_out, A_out);
  xor xor_2 (xor_2_out, B_out, and_1_out);
  D_Flip_Flop d_ff_1 (.clk(A_2_out), .D(d_ff_1_qn), .Q(d_ff_1_q), .Qn(d_ff_1_qn), .reset(R_2_out));  // open: preset, en
  LED led_1 (.in(d_ff_1_q));
  and and_1 (and_1_out, in_1, d_ff_8_q);
  D_Flip_Flop d_ff_2 (.clk(xor_1_out), .D(d_ff_2_qn), .Q(d_ff_2_q), .Qn(d_ff_2_qn), .reset(R_out));  // open: preset, en
  D_Flip_Flop d_ff_3 (.clk(xor_2_out), .D(d_ff_3_qn), .Q(d_ff_3_q), .Qn(d_ff_3_qn), .reset(R_out));  // open: preset, en
  D_Flip_Flop d_ff_4 (
    .clk(d_ff_1_qn), .D(d_ff_4_qn), .Q(d_ff_4_q), .Qn(d_ff_4_qn), .reset(R_2_out));  // open: preset, en
  LED led_2 (.in(d_ff_4_q));
  D_Flip_Flop d_ff_5 (.clk(d_ff_2_qn), .D(d_ff_5_qn), .Q(d_ff_5_q), .Qn(d_ff_5_qn), .reset(R_out));  // open: preset, en
  D_Flip_Flop d_ff_6 (.clk(d_ff_3_qn), .D(d_ff_6_qn), .Q(d_ff_6_q), .Qn(d_ff_6_qn), .reset(R_out));  // open: preset, en
  D_Flip_Flop d_ff_7 (
    .clk(d_ff_4_qn), .D(d_ff_7_qn), .Q(d_ff_7_q), .Qn(d_ff_7_qn), .reset(R_2_out));  // open: preset, en
  D_Flip_Flop d_ff_8 (.clk(d_ff_5_qn), .D(d_ff_8_qn), .Q(d_ff_8_q), .Qn(d_ff_8_qn), .reset(R_out));  // open: preset, en
  nand nand_1 (nand_1_out, d_ff_5_qn, d_ff_6_q);
  D_Flip_Flop d_ff_9 (.clk(d_ff_6_qn), .D(d_ff_9_qn), .Q(d_ff_9_q), .Qn(d_ff_9_qn), .reset(R_out));  // open: preset, en
  LED led_3 (.in(d_ff_7_q));
  and and_2 (and_2_out, d_ff_2_q, d_ff_5_q, d_ff_8_q);
  and and_3 (and_3_out, d_ff_9_q, d_ff_6_q, d_ff_3_q);
  Button A_3 (.out(A_3_out));
  Button B_2 (.out(B_2_out));
  or or_1 (or_1_out, and_2_out, and_3_out);
  and and_4 (and_4_out, d_ff_8_q, d_ff_9_qn);
  not not_1 (not_1_out, and_4_out);
  not not_2 (not_2_out, and_6_out);
  nand nand_2 (nand_2_out, d_ff_8_qn, d_ff_9_q);
  D_Flip_Flop d_ff_10 (.clk(A_3_out), .D(d_ff_10_qn), .Q(d_ff_10_q), .Qn(d_ff_10_qn));  // open: preset, en, reset
  and and_5 (and_5_out, d_ff_10_q, d_ff_11_qn);
  D_Flip_Flop d_ff_11 (.clk(B_2_out), .D(d_ff_11_qn), .Qn(d_ff_11_qn));  // open: Q, preset, en, reset
  not not_3 (not_3_out, or_1_out);
  and and_6 (and_6_out, not_1_out, d_ff_5_q, d_ff_6_qn, nand_2_out);
  or or_2 (or_2_out, and_4_out, and_6_out, and_7_out);
  and and_7 (and_7_out, not_2_out, not_1_out, nand_2_out, nand_1_out, d_ff_2_q, d_ff_3_qn);
  LED G (.in(and_5_out));
  LED E (.in(or_1_out));
  LED G_2 (.in(and_8_out));
  and and_8 (and_8_out, not_3_out, or_2_out);

  // Notes on the sheet:
  //   in_1: pull=up
  //   Toggle Overvlow to B register
  //   3 Bit counter (0-7)
  //   1Bit A > B Comparason
endmodule
